// Logisim project estacao_final_att.circ as structural Verilog: 1 circuit, main circuit main
module main (
);

  wire A, ALARME, and_1_out, and_2_out, and_3_out, and_4_out, and_5_out, and_6_out, and_8_out, and_9_out, B,
       C, not_1_out, not_2_out, not_3_out, not_4_out, or_1_out, or_2_out, or_3_out, or_4_out;

  Comparator #(.width(8), .mode("unsigned")) comparator_1 (.a(8'h17), .b(8'h1e), .gt(A));  // open: eq, lt
  Comparator #(.width(8), .mode("unsigned")) comparator_2 (.a(8'h20), .b(8'h1e), .lt(B));  // open: gt, eq
  Comparator #(.width(8), .mode("unsigned")) comparator_3 (.a(8'h20), .b(8'h50), .gt(C));  // open: eq, lt
  and and_1 (and_1_out, A, B);
  and and_2 (and_2_out, A, C);
  and and_3 (and_3_out, B, C);
  not not_1 (not_1_out, A);
  not not_2 (not_2_out, B);
  not not_3 (not_3_out, C);
  or or_1 (or_1_out, A, B);
  or or_2 (or_2_out, and_1_out, and_2_out);
  and and_4 (and_4_out, not_1_out, not_2_out);
  or or_3 (or_3_out, or_1_out, C);
  not not_4 (not_4_out, ALARME);
  or or_4 (or_4_out, or_2_out, and_3_out);
  and and_5 (and_5_out, and_4_out, not_3_out);
  and and_6 (and_6_out, or_3_out, not_4_out);
  and and_7 (ALARME, or_4_out, 1'b1);
  and and_8 (and_8_out, and_5_out, 1'b1);
  and and_9 (and_9_out, and_6_out, 1'b1);
  LED u_ALARME (.in(ALARME));
  LED NORMAL (.in(and_8_out));
  LED ATENCAO (.in(and_9_out));

  // Notes on the sheet:
  //   TEMP (0x17 = 23 C)
  //   UMID (0x20 = 32 %)
  //   LUZ (0x20 = 32 %)
  //   EN (0x1 = ligado)
endmodule
